# Fritzing sketch wemos (saved by Fritzing 0.9.3b)
circuit board: 3.61503cm x 2.87848cm
breadboards: 1

parts:
  WeMos_D1_Mini1 = WeMos D1 Mini
  J1 = female pin header, 5 pins [form="♀ (female)"]

nets:
  5V: WeMos_D1_Mini1.5V, J1.pin2
  N1: WeMos_D1_Mini1.D5, J1.pin5
  N2: WeMos_D1_Mini1.D6, J1.pin4
  N3: WeMos_D1_Mini1.D7, J1.pin3
  GND: WeMos_D1_Mini1.G, J1.pin1
